# Fritzing sketch Assignment1 (saved by Fritzing 0.9.3b)
breadboards: 1

parts:
  LED1 = LED - 5mm [color="Red (633nm)" package="5 mm [THT]"]
  Part1 = Arduino Uno (Rev3)
  LED2 = LED - 5mm [color="Red (633nm)" package="5 mm [THT]"]
  S1 = Pushbutton [package="[THT]"]

nets:
  N1: LED1.cathode, LED2.anode
  N2: LED1.anode, Part1.VIN
  N3: Part1.GND, LED2.cathode, S1.Pin_1, S1.Pin_2, S1.Pin_3, S1.Pin_4
